# Fritzing sketch Board de test avec des leds (saved by Fritzing 0.9.3b)
breadboards: 1

parts:
  LED1 = LED - 5mm [color="Red (633nm)" package="5 mm [THT]"]
  LED2 = LED - 5mm [color="Red (633nm)" package="5 mm [THT]"]
  LED3 = LED - 5mm [color="Blue (430nm)" package="5 mm [THT]"]
  LED4 = LED - 5mm [color="Blue (430nm)" package="5 mm [THT]"]
  LED5 = LED - 5mm [color="Green (555nm)" package="5 mm [THT]"]
  LED6 = LED - 5mm [color="Green (555nm)" package="5 mm [THT]"]
  Composant1 = Arduino Uno (Rev3)

nets:
  N1: LED1.cathode, LED2.cathode, LED3.cathode, LED4.cathode, LED5.cathode, LED6.cathode, Composant1.GND
  N2: LED1.anode, Composant1.D10_PWM/SS
  N3: LED2.anode, Composant1.D5_PWM
  N4: LED3.anode, Composant1.D9_PWM
  N5: LED4.anode, Composant1.D6_PWM
  N6: LED5.anode, Composant1.D8
  N7: LED6.anode, Composant1.D7
