# Fritzing sketch schéma_carrefour_potentiometre_bouton (saved by Fritzing 0.9.3b)
breadboards: 1

parts:
  Composant1 = Arduino Uno (Rev3)
  R1 = Resistor [tolerance=±5% resistance=220 package=THT]
  R2 = Resistor [tolerance=±5% resistance=220 package=THT]
  R3 = Resistor [tolerance=±5% resistance=220 package=THT]
  R4 = Resistor [tolerance=±5% resistance=220 package=THT]
  R5 = Resistor [tolerance=±5% resistance=220 package=THT]
  LED1 = LED - 5mm [color="Red (633nm)" package="5 mm [THT]"]
  LED2 = LED - 5mm [color="Red (633nm)" package="5 mm [THT]"]
  LED3 = LED - 5mm [color="Green (555nm)" package="5 mm [THT]"]
  LED4 = LED - 5mm [color="Green (555nm)" package="5 mm [THT]"]
  LED5 = LED - 5mm [color="Orange (605nm)" package="5 mm [THT]"]
  R6 = Trimmer Potentiometer [maximum_resistance=10kΩ package=THT]
  S1 = Pushbutton [package="[THT]"]
  LED6 = LED - 5mm [color="Red (633nm)" package="5 mm [THT]"]
  R7 = Resistor [tolerance=±5% resistance=220 package=THT]
  LED7 = LED - 5mm [color="Red (633nm)" package="5 mm [THT]"]
  R8 = Resistor [tolerance=±5% resistance=220 package=THT]

nets:
  N1: Composant1.A5/SCL, R6.wiper
  N2: Composant1.D8, R2.Pin_1
  N3: Composant1.D9_PWM, R1.Pin_1
  N4: Composant1.D10_PWM/SS, LED6.cathode
  N5: Composant1.D11_PWM/MOSI, R8.Pin_1
  N6: Composant1.D5_PWM, R5.Pin_1
  N7: Composant1.D6_PWM, R4.Pin_1
  N8: Composant1.D7, R3.Pin_1
  N9: Composant1.5V, R6.leg1, R7.Pin_0
  N10: Composant1.GND, LED1.anode, LED2.anode, LED3.anode, LED4.anode, LED5.anode, R6.leg2, LED7.anode
  N11: R1.Pin_0, LED2.cathode
  N12: R2.Pin_0, LED5.cathode
  N13: R3.Pin_0, LED4.cathode
  N14: R4.Pin_0, LED1.cathode
  N15: R5.Pin_0, LED3.cathode
  N16: S1.Pin_1, S1.Pin_2, R7.Pin_1
  N17: S1.Pin_3, S1.Pin_4, LED6.anode
  N18: LED7.cathode, R8.Pin_0
