# Fritzing sketch schéma_console_bouton_gpio (saved by Fritzing 0.9.3b)
breadboards: 1

parts:
  Composant1 = Arduino Uno (Rev3)
  S1 = Pushbutton [package="[THT]"]
  LED1 = LED - 5mm [color="Red (633nm)" package="5 mm [THT]"]
  R1 = Resistor [tolerance=±5% resistance=220 package=THT]

nets:
  N1: Composant1.D9_PWM, Composant1.GND, LED1.cathode
  N2: Composant1.5V, R1.Pin_1
  N3: S1.Pin_1, S1.Pin_2, R1.Pin_0
  N4: S1.Pin_3, S1.Pin_4, LED1.anode
