# Fritzing sketch schéma_console_potentiometre_analog (saved by Fritzing 0.9.3b)
breadboards: 1

parts:
  Composant1 = Arduino Uno (Rev3)
  R1 = Trimmer Potentiometer [maximum_resistance=10kΩ package=THT]

nets:
  N1: Composant1.A0, R1.wiper
  N2: Composant1.5V, R1.leg1
  N3: Composant1.GND, R1.leg2
