# Fritzing sketch joystick (saved by Fritzing 0.9.3b)
breadboards: 1

parts:
  Composant1 = Arduino Uno (Rev3)
  R3 = Resistor [tolerance=±5% resistance=220 package=THT]
  R4 = Resistor [tolerance=±5% resistance=220 package=THT]
  R5 = Resistor [tolerance=±5% resistance=220 package=THT]
  LED1 = LED - 5mm [color="Blue (430nm)" package="5 mm [THT]"]
  LED2 = LED - 5mm [color="Blue (430nm)" package="5 mm [THT]"]
  LED3 = LED - 5mm [color="Blue (430nm)" package="5 mm [THT]"]
  R6 = Resistor [tolerance=±5% resistance=220 package=THT]
  LED4 = LED - 5mm [color="Blue (430nm)" package="5 mm [THT]"]
  Composant2 = Thumb Joystick

nets:
  N1: Composant1.D8, R3.Pin_1
  N2: Composant1.D5_PWM, R6.Pin_1
  N3: Composant1.D6_PWM, R5.Pin_1
  N4: Composant1.D7, R4.Pin_1
  GND: Composant1.GND, LED1.anode, LED2.anode, LED3.anode, LED4.anode, Composant2.GND
  N5: R3.Pin_0, LED4.cathode
  N6: R4.Pin_0, LED1.cathode
  N7: R5.Pin_0, LED3.cathode
  N8: LED2.cathode, R6.Pin_0
