# Fritzing sketch led_fade (saved by Fritzing 0.9.3b)
breadboards: 1

parts:
  Composant1 = Arduino Uno (Rev3)
  R3 = Resistor [tolerance=±5% resistance=220 package=THT]
  R4 = Resistor [tolerance=±5% resistance=220 package=THT]
  R5 = Resistor [tolerance=±5% resistance=220 package=THT]
  LED1 = LED - 5mm [color="Red (633nm)" package="5 mm [THT]"]
  LED2 = LED - 5mm [color="Orange (620nm)" package="5 mm [THT]"]
  LED3 = LED - 5mm [color="Green (570nm)" package="5 mm [THT]"]
  R6 = Resistor [tolerance=±5% resistance=220 package=THT]
  LED4 = LED - 5mm [color="Blue (470nm)" package="5 mm [THT]"]

nets:
  N1: Composant1.D9_PWM, R3.Pin_1
  N2: Composant1.D5_PWM, R6.Pin_1
  N3: Composant1.D6_PWM, R5.Pin_1
  N4: Composant1.D7, R4.Pin_1
  N5: Composant1.GND, LED1.anode, LED2.anode, LED3.anode, LED4.anode
  N6: R3.Pin_0, LED4.cathode
  N7: R4.Pin_0, LED1.cathode
  N8: R5.Pin_0, LED3.cathode
  N9: LED2.cathode, R6.Pin_0
